// Logisim project decodsegg.circ as structural Verilog
module seg (
  input  d,
  input  c,
  input  b,
  input  a,
  output sa,
  output sb,
  output sc,
  output sd,
  output se,
  output sf,
  output sg
);

  wire and_1_out, and_2_out, and_3_out, and_4_out, and_5_out, and_6_out, and_7_out, and_8_out, and_9_out,
       and_10_out, and_11_out, and_12_out, and_13_out, and_14_out, and_15_out, and_16_out, not_1_out,
       not_2_out, not_3_out;

  not not_1 (not_1_out, c);
  not not_2 (not_2_out, b);
  not not_3 (not_3_out, a);
  and and_1 (and_1_out, a, c);
  and and_2 (and_2_out, not_3_out, not_1_out);
  and and_3 (and_3_out, not_3_out, not_2_out);
  and and_4 (and_4_out, a, b);
  or or_1 (sc, not_2_out, a, c);
  and and_5 (and_5_out, not_3_out, not_1_out);
  and and_6 (and_6_out, c, not_2_out, a);
  and and_7 (and_7_out, b, not_1_out);
  and and_8 (and_8_out, b, not_3_out);
  and and_9 (and_9_out, not_3_out, not_1_out);
  and and_10 (and_10_out, b, not_3_out);
  and and_11 (and_11_out, not_2_out, c);
  and and_12 (and_12_out, not_3_out, not_2_out);
  and and_13 (and_13_out, not_3_out, c);
  and and_14 (and_14_out, b, not_1_out);
  and and_15 (and_15_out, not_2_out, c);
  and and_16 (and_16_out, not_3_out, b);
  or or_2 (sa, and_1_out, b, and_2_out, d);
  or or_3 (sb, not_1_out, and_3_out, and_4_out);
  or or_4 (sd, and_5_out, d, and_6_out, and_7_out, and_8_out);
  or or_5 (se, and_9_out, and_10_out);
  or or_6 (sf, d, and_11_out, and_12_out, and_13_out);
  or or_7 (sg, d, and_14_out, and_15_out, and_16_out);
endmodule

module segsim (
  input  a,
  input  b,
  input  c,
  input  d
);

  wire seg_1_sa, seg_1_sb, seg_1_sc, seg_1_sd, seg_1_se, seg_1_sf, seg_1_sg;

  seg seg_1 (
    .d(a), .c(b), .b(c), .a(d), .sa(seg_1_sa), .sb(seg_1_sb), .sc(seg_1_sc), .sd(seg_1_sd), .se(seg_1_se),
    .sf(seg_1_sf), .sg(seg_1_sg));
  _7_Segment_Display L_7_Segment_Display_1 (
    .g(seg_1_sg), .f(seg_1_sf), .a(seg_1_sa), .b(seg_1_sb), .e(seg_1_se), .d(seg_1_sd), .c(seg_1_sc));  // open: dp
endmodule

module seggbasys (
  input  d,
  input  c,
  input  b,
  input  a,
  output an0,
  output sa,
  output sb,
  output an1,
  output sc,
  output an2,
  output sd,
  output an3,
  output se,
  output sf,
  output sg
);

  seg seg_1 (.d(d), .c(c), .b(b), .a(a), .sa(sa), .sb(sb), .sc(sc), .sd(sd), .se(se), .sf(sf), .sg(sg));

  assign an0 = 1'b1;
  assign an1 = 1'b0;
  assign an2 = 1'b0;
  assign an3 = 1'b0;
endmodule

module multiseg (
  input  d,
  input  c,
  input  b,
  input  a,
  output sa,
  output sb,
  output sc,
  output sd,
  output se,
  output sf,
  output sg
);

  wire and_1_out, and_2_out, and_3_out, and_4_out, and_5_out, and_6_out, and_7_out, and_8_out, and_9_out,
       and_10_out, and_11_out, and_12_out, and_13_out, and_14_out, and_15_out, and_16_out, not_1_out,
       not_2_out, not_3_out;

  not not_1 (not_1_out, c);
  not not_2 (not_2_out, b);
  not not_3 (not_3_out, a);
  and and_1 (and_1_out, a, c);
  and and_2 (and_2_out, not_3_out, not_1_out);
  and and_3 (and_3_out, not_3_out, not_2_out);
  and and_4 (and_4_out, a, b);
  or or_1 (sc, not_2_out, a, c);
  and and_5 (and_5_out, not_3_out, not_1_out);
  and and_6 (and_6_out, c, not_2_out, a);
  and and_7 (and_7_out, b, not_1_out);
  and and_8 (and_8_out, b, not_3_out);
  and and_9 (and_9_out, not_3_out, not_1_out);
  and and_10 (and_10_out, b, not_3_out);
  and and_11 (and_11_out, not_2_out, c);
  and and_12 (and_12_out, not_3_out, not_2_out);
  and and_13 (and_13_out, not_3_out, c);
  and and_14 (and_14_out, b, not_1_out);
  and and_15 (and_15_out, not_2_out, c);
  and and_16 (and_16_out, not_3_out, b);
  or or_2 (sa, and_1_out, b, and_2_out, d);
  or or_3 (sb, not_1_out, and_3_out, and_4_out);
  or or_4 (sd, and_5_out, d, and_6_out, and_7_out, and_8_out);
  or or_5 (se, and_9_out, and_10_out);
  or or_6 (sf, d, and_11_out, and_12_out, and_13_out);
  or or_7 (sg, d, and_14_out, and_15_out, and_16_out);
endmodule
